// Digital circuit Booth_multiplier1bit.dig as structural Verilog
module Booth_multiplier1bit (
  input  [3:0] multiplicand,
  input  [3:0] multiplier,
  output [7:0] product,
  output [3:0] s
);

  booth_multiplier1bit #(.applicationType("IVERILOG")) u_booth_multiplier1bit (
    .multiplicand(multiplicand), .multiplier(multiplier), .product(product), .s(s));
endmodule

/* Code of booth_multiplier1bit:
module booth_multiplier1bit(//一位乘
  input [3:0] multiplicand,//被乘数
  input [3:0] multiplier,//乘数
  output reg [7:0] product,
  output [3:0]s
);
  reg [8:0] p;
  reg [3:0] a;
  reg [3:0] b;
  reg [3:0] s;
  always @* begin
    a = multiplicand;b=multiplier;
    s = (~b)+1'b1; // 得到补码s
    p[4:1]=a;p[0]=1'b0;p[8:5]=4'b0000;
    repeat(4) begin
      if(p[1:0]==1)begin//对应后面两位“01”情况，执行加乘数移位操作
          p[8:5]=p[8:5]+b;
          p=p>>1;
          p[8]=p[7];
      end
      else if(p[1:0]==2)begin//对应后面两位“10”情况，执行减乘数移位操作（加补码）
         p[8:5]=p[8:5]+s;
         p=p>>1;
         p[8]=p[7];
      end
      else begin//0011情况直接移位
      p=p>>1;
      p[8]=p[7];
      end
    end
  product=p[8:1];
  end
endmodule
*/

/* Test case:
multiplicand multiplier product s
0b0100 0b0110 0b00011000 0b1010
0b0100 0b0100 0b00010000 0b1100
0b0101 0b0111 0b00100011 0b1001
0b0001 0b0001 0b00000001 0b1111
*/
