// Digital circuit fully_associative_cache_v.dig as structural Verilog
module fully_associative_cache_v (
  input  [7:0] address,
  input  write_enable,
  input  [7:0] data_in,
  input  clk,
  output [7:0] data_out,
  output hit,
  output [1:0] row
);

  fully_associative_cache #(.applicationType("IVERILOG")) u_fully_associative_cache (
    .address(address), .write_enable(write_enable), .data_in(data_in), .clk(clk), .data_out(data_out),
    .hit(hit), .row(row));
endmodule

/* Code of fully_associative_cache:
module fully_associative_cache(
    input wire [7:0] address,
    input wire write_enable,
    input wire [7:0] data_in,
    input clk,
    output reg [7:0] data_out,
    output reg hit,
    output reg [1:0] row
);
parameter num_lines = 4; // cache的行数
parameter tag_width = 4; // 标记位的宽度
reg [7:0] cache_data [0:num_lines-1]; // cache数据存储
reg [tag_width-1:0] tag [0:num_lines-1]; // 标记位存储
reg valid [0:num_lines-1]; // 有效位
reg [tag_width-1:0] tagcount [0:num_lines-1];//标记位计数
reg [tag_width-1:0] address_tag;
integer i,j,max;
initial begin
for(i=0;i<4;i=i+1)begin
   valid[i]=0;tagcount[i]=0;
   end
i=0;j=0;max=0;
end

always @(posedge clk) begin
    data_out=0;address_tag = address[7:4]; // 从地址中提取标记位
    hit = 0; row=0;// 初始化未命中
    if (write_enable) begin // 如果是写操作
        for (i = 0; i < num_lines; i = i + 1) begin
            if (!valid[i] || tag[i] == address_tag) begin // 找到一个无效行
                cache_data[i] = data_in; // 写入数据
                tag[i] = address_tag; // 更新标记位
                valid[i] = 1; // 设置有效位
                row=i;i=num_lines;//row行命中，剩下的行不做判断退出
            end
        end
        if(i==num_lines)begin//此时未命中所有行都读完了，必须读入新的数据
            for (j = num_lines-1; j >= 0; j = j - 1) begin
            if(max<tagcount[j])begin
               max=j;
               end//找到计数最大的行数
            end
            cache_data[max] = data_in; // 写入数据
                tag[max] = address_tag; // 更新标记位
                valid[max] = 1; // 设置有效位
                row=max;
        end
    end 
    else begin // 如果是读操作
        for (i = 0; i < num_lines; i = i + 1) begin
            if (valid[i] && tag[i] == address_tag) begin // 如果命中
                data_out = cache_data[i]; // 从cache中读取数据
                hit = 1; // 设置命中标志
                row=i;
            end
        end
        
        for (j=0;j<num_lines;j=j+1 )begin
             if(j!=row)begin
             tagcount[j]=tagcount[j]+1;//当前行数计数
             end
             else tagcount[j]=0;
        end
    end
end
endmodule
*/

/* Test case:
address    write_enable data_in    data_out   hit row clk
0b00010001 1            0b00011101 0b00000000 0 0 C
0b00110010 1            0b00010001 0b00000000 0 1 C
0b00010001 0            0b00011101 0b00011101 1 0 C
0b00110010 0            0b00010001 0b00010001 1 1 C
0b01010010 1            0b00010101 0b00000000 0 0b10 C
0b01010010 1            0b00010111 0b00000000 0 0b10 C
0b01010010 0            0b00010001 0b00010111 1 0b10 C
0b01010010 0            0b00010001 0b00010111 1 0b10 C
0b10010010 1            0b00010011 0b00000000 0 0b11 C
0b10110010 1            0b00010011 0b00000000 0 0b11 C
0b10110010 0            0b00010011 0b00010011 1 0b11 C
*/
