// Digital circuit stack4bit_v.dig as structural Verilog
module stack4bit_v (
  input  [3:0] data_in,
  input  pushpop,
  input  clk,
  output [3:0] data_out,
  output full,
  output empty
);

  stack4bit #(.applicationType("IVERILOG")) u_stack4bit (
    .data_in(data_in), .pushpop(pushpop), .clk(clk), .data_out(data_out), .full(full), .empty(empty));
endmodule

/* Code of stack4bit:
module stack4bit(
    input wire [3:0] data_in,
    input wire pushpop,
    input clk,
    output reg [3:0] data_out,
    output reg full,
    output reg empty
);

reg [3:0] memory [0:7]; // 堆栈内存，共8个位置
reg top; // 堆栈指针

initial begin
    top = 0; // 初始化堆栈指针
    full = 0; // 堆栈初始为空
    empty = 1;
end

always @(posedge clk) begin
    data_out=0;
    if (pushpop && !full) begin // 如果要push数据且堆栈不满
        memory[top] = data_in; // 将数据写入堆栈
        top = top + 1'b1; // 堆栈指针加1
        if (top == 7)begin // 如果堆栈指针达到最大值
            full = 1;
            end // 堆栈满
        empty = 0; // 堆栈不为空
    end else if (!pushpop && !empty) begin // 如果要pop数据且堆栈不空
        top = top - 1'b1; // 堆栈指针减1
        data_out = memory[top]; // 从堆栈中取出数据
        if (top == 0)begin // 如果堆栈指针为0
            empty = 1;
            end // 堆栈为空
        full = 0; // 堆栈不满
    end
end

endmodule
*/

/* Test case:
clk data_in pushpop data_out full empty
C 0b1001  1   0b0000   0    0
C 0b1010  0   0b1001   0    1
C 0b0101  1   0b0000   0    0
C 0b0001  0   0b0101   0    1
C 0b0101  1   0b0000   0    0
C 0b0110  1   0b0000   0    0
C 0b0001  0   0b0110   0    0
C 0b0001  0   0b0101   0    1
*/
