// Digital circuit CRC_v.dig as structural Verilog
module CRC_v (
  input  [9:0] data,
  output [3:0] crc,
  output work
);

  CRC #(.applicationType("IVERILOG")) u_CRC (.data(data), .work(work), .crc(crc));
endmodule

/* Code of CRC:
module CRC(
input [9:0] data,//信息码10位
output reg [3:0] crc,//crc-4校验码
output work
    );
    reg work=0;
    wire [3:0] crc_temp;//crc校验结果寄存器
    reg [13:0] temp    ;//移位数据用于除法运算
    parameter gx=5'b1_0011;//生成多项式
    always@(*)begin
                begin
                crc=4'd0;  		
    		temp={data[9:0],4'b0};
                work=1;
                end
    		if(temp[13]==1'd1)begin //高位为1 进行异或
    				temp[13:9]=temp[13:9]^gx;//从高到低依次取5位（和gx同位宽）进行异或
    		end
    		if(temp[12]==1'd1)begin
    				temp[12:8]=temp[12:8]^gx;
    		end
    		if(temp[11]==1'd1)begin
    				temp[11:7]=temp[11:7]^gx;
    		end
    		if(temp[10]==1'd1)begin
    				temp[10:6]=temp[10:6]^gx;
    		end
    		if(temp[9]==1'd1)begin
    				temp[9:5]=temp[9:5]^gx;
    		end
    		if(temp[8]==1'd1)begin
    				temp[8:4]=temp[8:4]^gx;
    		end
    		if(temp[7]==1'd1)begin
    				temp[7:3]=temp[7:3]^gx;
    		end
    		if(temp[6]==1'd1)begin
    				temp[6:2]=temp[6:2]^gx;
    		end
    		if(temp[5]==1'd1)begin
    				temp[5:1]=temp[5:1]^gx;
    		end
    		if(temp[4]==1'd1)begin
    				temp[4:0]=temp[4:0]^gx;
    		end
    		begin
    			crc=temp[3:0];//取出余数
    		end
    end
    assign crc_temp={data[9:0],crc[3:0]};
endmodule
*/

/* Test case:
data          crc    work
0b1011000111  0b1101 1
0b1101010101  0b1111 1
0b1101010110  0b1010 1
*/
