// Digital circuit hamming_v.dig as structural Verilog
module hamming_v (
  input  [5:0] A,
  input  [9:0] B,
  output [9:0] X,
  output [3:0] error
);

  hamming #(.applicationType("IVERILOG")) u_hamming (.data_in(A), .num(B), .data_out(X), .Error(error));
endmodule

/* Code of hamming:
module hamming (
output [9: 0]data_out,
output [3: 0]Error,
input [9: 0] num,
input [5: 0] data_in
);
wire [3:0]error;
	assign data_out[9]=data_in[5]^data_in[4]^data_in[2]^data_in[1];
        assign data_out[8]=data_in[5]^data_in[3]^data_in[2]^data_in[0];
        assign data_out[6]=data_in[4]^data_in[3]^data_in[2];
        assign data_out[2]=data_in[1]^data_in[0];
        assign data_out[7]=data_in[5];
        assign data_out[5]=data_in[4];
        assign data_out[4]=data_in[3];
        assign data_out[3]=data_in[2];
        assign data_out[1]=data_in[1];
        assign data_out[0]=data_in[0];
        assign error[0]=num[0]^num[2]^num[4]^num[6]^num[8];
        assign error[1]=num[1]^num[2]^num[5]^num[6]^num[9];
        assign error[2]=num[3]^num[4]^num[5]^num[6];
        assign error[3]=num[7]^num[8]^num[9];
        assign Error=error;
endmodule
*/

/* Test case:
A B X error
0 0x2E4 0 0
1 0x2E5 0x105 1
2 0x2E6 0x206 2
3 0x2E0 0x303 3
4 0x2EC 0x348 4
5 0x2F4 0x24D 5
7 0x2A4 0x4B 7
*/
