// Digital circuit Booth_multiplier2bit.dig as structural Verilog
module Booth_multiplier2bit (
  input  [3:0] multiplicand,
  input  [3:0] multiplier,
  output [7:0] product,
  output [3:0] s
);

  booth_multiplier2bit #(.applicationType("IVERILOG")) u_booth_multiplier2bit (
    .multiplicand(multiplicand), .multiplier(multiplier), .product(product), .s(s));
endmodule

/* Code of booth_multiplier2bit:
module booth_multiplier2bit(//二位乘
  input [3:0] multiplicand,//被乘数
  input [3:0] multiplier,//乘数
  output reg [7:0] product,
  output [3:0]s
);
  reg [8:0] p;
  reg [3:0] a;
  reg [3:0] b;
  reg [3:0] s;
  always @* begin
    a = multiplicand;b=multiplier;
    s = (~b)+1'b1; // 得到补码s
    p[4:1]=a;p[0]=1'b0;p[8:5]=4'b0000;
    repeat(2) begin
      if(p[0]+p[1]-p[2]-p[2]==1)begin//执行加1倍乘数移位操作
          p[8:5]=p[8:5]+b;
      end
      else if(p[0]+p[1]-p[2]-p[2]==2)begin//执行加2倍乘数移位操作
          p[8:5]=p[8:5]+b+b;
      end
      else if(p[0]+p[1]-p[2]-p[2]==-1)begin//执行减1倍乘数移位操作
          p[8:5]=p[8:5]-b;
      end
      else if(p[0]+p[1]-p[2]-p[2]==-2)begin//执行减2倍乘数移位操作
          p[8:5]=p[8:5]-b-b;
      end
      p=p>>2;
      p[7]=p[6];
      p[8]=p[6];
    end
  p[8]=0;p[7]=0;//前面的逻辑移位多移了一次，最后补0，以免出现错误
  product=p[8:1];
  end
endmodule
*/

/* Test case:
multiplicand multiplier product s
0b0100 0b0110 0b00011000 0b1010
0b0100 0b0100 0b00010000 0b1100
0b0101 0b0111 0b00100011 0b1001
0b0001 0b0001 0b00000001 0b1111
*/
