// Digital circuit Divider_v.dig as structural Verilog
module Divider_v (
  input  [7:0] dividend,
  input  [3:0] divisor,
  output [3:0] quotient,
  output [3:0] remainder
);

  Divider_v #(.applicationType("IVERILOG")) u_Divider_v (
    .dividend(dividend), .divisor(divisor), .quotient(quotient), .remainder(remainder));
endmodule

/* Code of Divider_v:
module Divider_v(//普通除法器
  input [7:0] dividend,
  input [3:0] divisor,
  output reg [3:0] quotient,
  output reg [3:0] remainder
);
    reg [7:0] temp_dividend;
    reg [3:0] temp_quotient;
    reg [3:0] temp_remainder;
  always @(*) begin
    temp_dividend = dividend;
    temp_quotient = 4'b0;
    temp_remainder = 4'b0;
    for (integer i = 0; i < 8; i = i + 1) begin
      temp_remainder = {temp_remainder[2:0], temp_dividend[7]};//临时的余数
      temp_dividend = temp_dividend << 1;//每次除完都移1位
      if (temp_remainder >= divisor) begin
        temp_remainder = temp_remainder - divisor;
        temp_quotient[7-i] = 1;//商的最后需要倒过来表示，高位先得
      end
    end
    quotient = temp_quotient;remainder = temp_remainder;
  end
endmodule
*/

/* Test case:
dividend   divisor quotient remainder
0b00001010 0b0101  0b0010   0b0000
0b00001010 0b0100  0b0010   0b0010
*/
