// Digital circuit SRTDivider.dig as structural Verilog
module SRTDivider (
  input  [7:0] dividend,
  input  [3:0] divisor,
  output [3:0] quotient,
  output [7:0] remainder
);

  SRTDivider #(.applicationType("IVERILOG")) u_SRTDivider (
    .dividend(dividend), .divisor(divisor), .quotient(quotient), .remainder(remainder));
endmodule

/* Code of SRTDivider:
module SRTDivider (
    input [7:0] dividend,
    input [3:0] divisor,
    output reg [3:0] quotient,
    output reg [7:0] remainder
);
    reg [7:0] A;
    reg [7:0] B;
    reg [3:0] Q;
    integer i,k,j;
always @(*) begin
    A = dividend;A[0]=0;B[7:4]=0;B[3:0]=divisor[3:0];
    for(k=0;(B[6]==0)&k<8;k=k+1)begin//一直移动除数让左第二位为1，记录移位次数
    B=B<<1;B[0]=0;
    end
    for(j=k-4;j>0;j=j-1)begin//被除数移位到与除数移位次数k相差为4次
    A=A<<1;A[0]=0;
    end
    Q = 0;
    for (i=0; i < 4; i = i + 1) begin//循环4次判断
          A=A<<1;A[0]=0;
          if(A[7:6]==2'b01)begin//此时为“01”，大于1/2，减去
          A=A-B; Q[3-i]=1'b1;
          end
          else if(A[7:6]==2'b10)begin//此时为“10”，小于-1/2，加上
          A=A+B;
          end
       end
       if(A[7]==1'b1)begin//如果得到商最高位为1则要加上除数，商减1（商的检查）
       A=A+B;quotient=Q-1; 
       end
       else begin
       quotient=Q;
       end
       for(integer s=k;s>0;s=s-1)begin//最后记得把得到的余数右移位k次
       A=A>>1;
       A[7]=0;
       end
       remainder=A;
end
endmodule
*/

/* Test case:
dividend   divisor quotient remainder
0b00001010 0b0101  0b0010   0b0000
0b00001010 0b0100  0b0010   0b0010
*/
