// Digital circuit fifo4bit_v.dig as structural Verilog
module fifo4bit_v (
  input  [3:0] data_in,
  input  push,
  input  pop,
  input  clk,
  output [3:0] data_out,
  output full,
  output empty
);

  fifo4bit #(.applicationType("IVERILOG")) u_fifo4bit (
    .data_in(data_in), .push(push), .pop(pop), .clk(clk), .data_out(data_out), .full(full), .empty(empty));
endmodule

/* Code of fifo4bit:
module fifo4bit(
    input wire [3:0] data_in,
    input wire push,
    input wire pop,
    input clk,
    output reg [3:0] data_out,
    output reg full,
    output reg empty
);

reg [3:0] memory [0:7]; // FIFO内存，共8个位置
integer head, tail; // FIFO头指针和尾指针

initial begin
    head = 0; // 初始化头指针
    tail = 0; // 初始化尾指针
    full = 0; // FIFO初始为空
    empty = 1;
end

always @(posedge clk) begin
    data_out=0;
    if (push && !full) begin // 如果要push数据且FIFO不满
        memory[head] = data_in; // 将数据写入FIFO
        head = head + 1; // 头指针加1
        if (head == 8)begin // 如果头指针达到最大值
            head = 0;
            end // 回绕到数组开头
        if (head == tail)begin // 如果头指针追上尾指针
            full = 1; // FIFO满
            end
        else begin
            full=0;
            end
        empty = 0; // FIFO不为空
    end
    if (pop && !empty) begin // 如果要pop数据且FIFO不空
        data_out = memory[tail]; // 从FIFO中取出数据
        tail = tail + 1; // 尾指针加1
        if (tail == 8)begin // 如果尾指针达到最大值
            tail = 0;
            end // 回绕到数组开头
        if (head == tail)begin // 如果头指针赶上尾指针
            empty = 1; // FIFO为空
            end
        else begin
            empty=0;
            end
        full = 0; // FIFO不满
    end
end

endmodule
*/

/* Test case:
data_in push pop data_out full empty clk
0b0001  1    1   0b0001   0    1 C
0b0010  1    0   0b0000   0    0 C
0b0011  1    0   0b0000   0    0 C
0b0100  1    0   0b0000   0    0 C
0b0101  1    0   0b0000   0    0 C
0b0110  1    0   0b0000   0    0 C
0b0111  1    0   0b0000   0    0 C
0b1000  1    0   0b0000   0    0 C
0b1001  1    0   0b0000   1    0 C
0b1001  0    1   0b0010   0    0 C
0b1001  1    1   0b0011   0    0 C
*/
