// Digital circuit 实验一 运算器.dig as structural Verilog
module \实验一_运算器  (
  input  K0,
  input  K1,
  input  K2,
  input  K3,
  input  K4,
  input  K5,
  input  K6,
  input  K7,
  input  K8,
  input  K9,
  input  K10,
  input  K11,
  input  K12,
  input  K13,
  input  K14,
  input  K15,
  input  SD0,
  input  SD1,
  input  SD2,
  input  SD3,
  input  SD4,
  input  SD5,
  input  SD6,
  input  SD7,
  input  T3
);

  wire _74181_2_pin7, A0, A1, A2, A3, A4, A5, A6, A7, and_1_out, and_2_out, and_3_out, and_4_out, B0, B1, B2,
       B3, B4, B5, B6, B7, C, D0, D1, D2, D3, D4, D5, D6, D7, F0, F1, F2, F3, F4, F5, F6, F7, LR0, LR1, LR2,
       LR3, undriven, undriven_2, Z;
  wire [7:0] DBUS, R0, R1, R2, R3;

  Multiplexer #(.Bits(8)) multiplexer_1 (
    .sel(K3), .in_0(DBUS), .in_1({SD7, SD6, SD5, SD4, SD3, SD2, SD1, SD0}),
    .out({D7, D6, D5, D4, D3, D2, D1, D0}));
  Multiplexer #(.Selector_Bits(2), .Bits(8)) multiplexer_2 (
    .sel({K6, K5}), .in_0(R0), .in_1(R1), .in_2(R2), .in_3(R3), .out({A7, A6, A5, A4, A3, A2, A1, A0}));
  Multiplexer #(.Selector_Bits(2), .Bits(8)) multiplexer_3 (
    .sel({K2, K1}), .in_0(R0), .in_1(R1), .in_2(R2), .in_3(R3), .out({B7, B6, B5, B4, B3, B2, B1, B0}));
  Register #(.Bits(8)) u_R0 (.D({D7, D6, D5, D4, D3, D2, D1, D0}), .C(T3), .en(and_1_out), .Q(R0));
  and and_1 (and_1_out, LR0, K4);
  Register #(.Bits(8)) u_R1 (.D({D7, D6, D5, D4, D3, D2, D1, D0}), .C(T3), .en(and_2_out), .Q(R1));
  and and_2 (and_2_out, LR1, K4);
  Register #(.Bits(8)) u_R2 (.D({D7, D6, D5, D4, D3, D2, D1, D0}), .C(T3), .en(and_3_out), .Q(R2));
  and and_3 (and_3_out, LR2, K4);
  Register #(.Bits(8)) u_R3 (.D({D7, D6, D5, D4, D3, D2, D1, D0}), .C(T3), .en(and_4_out), .Q(R3));
  and and_4 (and_4_out, LR3, K4);
  Decoder #(.Selector_Bits(2)) decoder_1 (.sel({K6, K5}), .out_0(LR0), .out_1(LR1), .out_2(LR2), .out_3(LR3));
  _74181 _74181_1 (
    .pin1(B0), .pin2(A0), .pin3(K14), .pin4(K13), .pin5(K12), .pin6(K11), .pin7(K10), .pin8(K15), .pin9(F0),
    .pin10(F1), .pin11(F2), .pin12(1'b0));  // open: pin13, pin14, pin15, pin16, pin17, pin18, pin19, pin20, pin21, pin22, pin23, pin24
  _74181 _74181_2 (
    .pin1(B4), .pin2(A4), .pin3(K14), .pin4(K13), .pin5(K12), .pin6(K11), .pin7(_74181_2_pin7), .pin8(K15),
    .pin9(F4), .pin10(F5), .pin11(F6), .pin12(1'b0));  // open: pin13, pin14, pin15, pin16, pin17, pin18, pin19, pin20, pin21, pin22, pin23, pin24
  Register u_C (.D(undriven), .C(T3), .en(K8), .Q(C));
  Register u_Z (.D(undriven_2), .C(T3), .en(K7), .Q(Z));
  Register #(.Bits(8)) u_DBUS (.D({F7, F6, F5, F4, F3, F2, F1, F0}), .C(T3), .en(K9), .Q(DBUS));

  // Other names for the same wires on the sheet: ABUS = K9; CIN = K10; DRW = K4; LDC = K8; LDZ = K7; M = K15;
  //   MBUS = K0; RD0 = K5; RD1 = K6; RS0 = K1; RS1 = K2; S0 = K11; S1 = K12; S2 = K13; S3 = K14; SBUS = K3
endmodule
