// Digital circuit 简易CPU架构.dig as structural Verilog
module \简易CPU架构  (
  input  INT,
  input  SWC,
  input  SWB,
  input  SWA,
  input  SD0,
  input  SD1,
  input  SD2,
  input  SD3,
  input  SD4,
  input  SD5,
  input  SD6,
  input  SD7,
  input  T3,
  input  T2,
  input  CLR
);

  wire _74181_2_pin7, A0, A1, A2, A3, A4, A5, A6, A7, ABUS, and_2_out, and_3_out, and_4_out, and_5_out,
       and_6_out, and_7_out, and_8_out, and_9_out, and_10_out, and_11_out, and_12_out, and_13_out,
       and_14_out, and_15_out, ARINC, B0, B1, B2, B3, B4, B5, B6, B7, C, CIN, D0, D1, D2, D3, D4, D5, D6, D7,
       DRW, F0, F1, F2, F3, F4, F5, F6, F7, IABUS, INTDI, INTEN, LAR, LDC, LDZ, LIAR, LIR, LPC, LR0, LR1,
       LR2, LR3, M, MBUS, MEMW, not_1_out, not_2_out, or_2_out, P0, P1, P2, P3, P4, PCADD, PCINC, RD0, RD1,
       RS0, RS1, S0, S1, S2, S3, SBUS, SEL0, SEL1, SEL2, SEL3, SELCTL, STOP, T2_t, T3_t, uA0, uA1, uA2, uA3,
       uA4, uA5, undriven, undriven_2, Z;
  wire [4:0] or_3_out;
  wire [5:0] MAR_q, multiplexer_12_out;
  wire [7:0] add_1_s, add_2_s, AR, DBUS, DBUSF, IAR_q, IBUS, IR, multiplexer_2_out, multiplexer_6_out,
       multiplexer_7_out, multiplexer_8_out, multiplexer_9_out, multiplexer_10_out, multiplexer_11_out, PC,
       R0, R1, R2, R3;

  and and_1 (T2_t, T2, not_1_out);
  not not_1 (not_1_out, CLR);
  or or_1 (T3_t, CLR, T3);
  Multiplexer #(.Bits(4)) multiplexer_1 (
    .sel(SELCTL), .in_0(IR[3:0]), .in_1({SEL3, SEL2, SEL1, SEL0}), .out({RD1, RD0, RS1, RS0}));
  Multiplexer #(.Bits(8)) multiplexer_2 (.sel(ABUS), .in_0(DBUS), .in_1(DBUSF), .out(multiplexer_2_out));
  Multiplexer #(.Bits(8)) multiplexer_3 (
    .sel(SBUS), .in_0(multiplexer_2_out), .in_1({SD7, SD6, SD5, SD4, SD3, SD2, SD1, SD0}),
    .out({D7, D6, D5, D4, D3, D2, D1, D0}));
  Multiplexer #(.Selector_Bits(2), .Bits(8)) multiplexer_4 (
    .sel({RD1, RD0}), .in_0(R0), .in_1(R1), .in_2(R2), .in_3(R3), .out({A7, A6, A5, A4, A3, A2, A1, A0}));
  Multiplexer #(.Selector_Bits(2), .Bits(8)) multiplexer_5 (
    .sel({RS1, RS0}), .in_0(R0), .in_1(R1), .in_2(R2), .in_3(R3), .out({B7, B6, B5, B4, B3, B2, B1, B0}));
  Register #(.Bits(8)) u_IR (.D(IBUS), .C(T3_t), .en(LIR), .Q(IR));
  Register #(.Bits(8)) IAR (.D(PC), .C(T3_t), .en(LIAR), .Q(IAR_q));
  Register #(.Bits(8)) u_R0 (.D({D7, D6, D5, D4, D3, D2, D1, D0}), .C(T3_t), .en(and_2_out), .Q(R0));
  and and_2 (and_2_out, LR0, DRW);
  Register #(.Bits(8)) u_R1 (.D({D7, D6, D5, D4, D3, D2, D1, D0}), .C(T3_t), .en(and_3_out), .Q(R1));
  and and_3 (and_3_out, LR1, DRW);
  Register #(.Bits(8)) u_R2 (.D({D7, D6, D5, D4, D3, D2, D1, D0}), .C(T3_t), .en(and_4_out), .Q(R2));
  and and_4 (and_4_out, LR2, DRW);
  Register #(.Bits(8)) u_R3 (.D({D7, D6, D5, D4, D3, D2, D1, D0}), .C(T3_t), .en(and_5_out), .Q(R3));
  and and_5 (and_5_out, LR3, DRW);
  Decoder #(.Selector_Bits(2)) decoder_1 (.sel({RD1, RD0}), .out_0(LR0), .out_1(LR1), .out_2(LR2), .out_3(LR3));
  // Probe on IR
  // Probe on IAR_q
  RAMDualAccess #(.AddrBits(8), .Bits(8)) ramdualaccess_1 (
    .str(MEMW), .C(T2_t), .ld(MBUS), .A1(AR), .Din1({D7, D6, D5, D4, D3, D2, D1, D0}), .A2(PC), .D1(DBUS),
    .D2(IBUS));
  Multiplexer #(.Bits(8)) multiplexer_6 (.sel(LPC), .in_0(add_1_s), .in_1({4'b0000, IR[3:0]}), .out(multiplexer_6_out));
  Multiplexer #(.Bits(8)) multiplexer_7 (
    .sel(IABUS), .in_0({D7, D6, D5, D4, D3, D2, D1, D0}), .in_1(IAR_q), .out(multiplexer_7_out));
  // Probe on multiplexer_6_out
  Multiplexer #(.Bits(8)) multiplexer_8 (.sel(LAR), .in_0(add_2_s), .in_1(multiplexer_7_out), .out(multiplexer_8_out));
  _74181 _74181_1 (
    .pin1(B0), .pin2(A0), .pin3(S3), .pin4(S2), .pin5(S1), .pin6(S0), .pin7(CIN), .pin8(M), .pin9(F0),
    .pin10(F1), .pin11(F2), .pin12(1'b0));  // open: pin13, pin14, pin15, pin16, pin17, pin18, pin19, pin20, pin21, pin22, pin23, pin24
  _74181 _74181_2 (
    .pin1(B4), .pin2(A4), .pin3(S3), .pin4(S2), .pin5(S1), .pin6(S0), .pin7(_74181_2_pin7), .pin8(M),
    .pin9(F4), .pin10(F5), .pin11(F6), .pin12(1'b0));  // open: pin13, pin14, pin15, pin16, pin17, pin18, pin19, pin20, pin21, pin22, pin23, pin24
  Multiplexer #(.Bits(8)) multiplexer_9 (
    .sel(CLR), .in_0(multiplexer_6_out), .in_1({8{1'b0}}), .out(multiplexer_9_out));
  or or_2 (or_2_out, CLR, PCINC);
  Multiplexer #(.Bits(8)) multiplexer_10 (
    .sel(CLR), .in_0(multiplexer_8_out), .in_1({8{1'b0}}), .out(multiplexer_10_out));
  Register #(.Bits(8)) u_PC (.D(multiplexer_9_out), .C(T3), .en(or_2_out), .Q(PC));
  not not_2 (not_2_out, CLR);
  Multiplexer #(.Bits(8)) multiplexer_11 (
    .sel(PCADD), .in_0(8'h1), .in_1({D7, D6, D5, D4, D3, D2, D1, D0}), .out(multiplexer_11_out));
  Register #(.Bits(8)) u_AR (.D(multiplexer_10_out), .C(T3_t), .en(not_2_out), .Q(AR));
  // Probe on PC
  Add #(.Bits(8)) add_1 (.a(PC), .b(multiplexer_11_out), .c_i(1'b0), .s(add_1_s));  // open: c_o
  // Probe on AR
  Register u_C (.D(undriven_2), .C(T3_t), .en(LDC), .Q(C));
  Register u_Z (.D(undriven), .C(T3_t), .en(LDZ), .Q(Z));
  Register #(.Bits(8)) u_DBUS (.D({F7, F6, F5, F4, F3, F2, F1, F0}), .C(~T3_t), .en(ABUS), .Q(DBUSF));
  and and_6 (and_6_out, INT, P4);
  and and_7 (and_7_out, SWC, P0);
  and and_8 (and_8_out, IR[7], P1);
  and and_9 (and_9_out, SWB, P0);
  and and_10 (and_10_out, IR[6], P1);
  and and_11 (and_11_out, SWA, P0);
  and and_12 (and_12_out, IR[5], P1);
  and and_13 (and_13_out, Z, P3);
  and and_14 (and_14_out, C, P2);
  and and_15 (and_15_out, IR[4], P1);
  or or_3 (or_3_out[4], and_6_out, uA4);
  or or_4 (or_3_out[3], and_7_out, uA3, and_8_out);
  or or_5 (or_3_out[2], and_9_out, uA2, and_10_out);
  or or_6 (or_3_out[1], and_11_out, uA1, and_12_out);
  or or_7 (or_3_out[0], and_13_out, and_14_out, uA0, and_15_out);
  Add #(.Bits(8)) add_2 (.a({8{1'b0}}), .b(AR), .c_i(ARINC), .s(add_2_s));  // open: c_o
  // Probe on {uA5, or_3_out}
  Multiplexer #(.Bits(6)) multiplexer_12 (
    .sel(CLR), .in_0({uA5, or_3_out}), .in_1({6{1'b0}}), .out(multiplexer_12_out));
  Register #(.Bits(6)) MAR (.D(multiplexer_12_out), .C(~T3), .en(1'b1), .Q(MAR_q));
  ROM #(.AddrBits(6), .Bits(8), .Addr_Bits(6)) CM0 (.A(MAR_q), .sel(1'b1), .D({P1, P0, uA5, uA4, uA3, uA2, uA1, uA0}));
  ROM #(.AddrBits(6), .Bits(8), .Addr_Bits(6)) CM1 (
    .A(MAR_q), .sel(1'b1), .D({LAR, ARINC, LPC, PCINC, DRW, P4, P3, P2}));
  ROM #(.AddrBits(6), .Bits(8), .Addr_Bits(6)) CM2 (
    .A(MAR_q), .sel(1'b1), .D({S1, S0, CIN, LDC, LDZ, LIR, STOP, MEMW}));
  ROM #(.AddrBits(6), .Bits(8), .Addr_Bits(6)) CM3 (
    .A(MAR_q), .sel(1'b1), .D({LIAR, IABUS, MBUS, SBUS, ABUS, M, S3, S2}));
  ROM #(.AddrBits(6), .Bits(8), .Addr_Bits(6)) CM4 (
    .A(MAR_q), .sel(1'b1), .D({PCADD, SELCTL, SEL3, SEL2, SEL1, SEL0, INTEN, INTDI}));
  // Probe on MAR_q
  // Probe on {P1, P0, uA5, uA4, uA3, uA2, uA1, uA0}
  // Probe on {LAR, ARINC, LPC, PCINC, DRW, P4, P3, P2}
  // Probe on {S1, S0, CIN, LDC, LDZ, LIR, STOP, MEMW}
  // Probe on {LIAR, IABUS, MBUS, SBUS, ABUS, M, S3, S2}
  // Probe on {PCADD, SELCTL, SEL3, SEL2, SEL1, SEL0, INTEN, INTDI}

  // Other names for the same wires on the sheet: INS0 = IBUS[0]; INS1 = IBUS[1]; INS2 = IBUS[2]; INS3 = IBUS[3];
  //   INS4 = IBUS[4]; INS5 = IBUS[5]; INS6 = IBUS[6]; INS7 = IBUS[7]; T33 = T3

  // Notes on the sheet:
  //   contents of CM0 (hex, n*v repeats v):
  //   41,a0,2,2,4,4,0,6,a,8,c,0,0,0,0,0,1,14,1,1,1,0,0,0,0,0,0,0,0,0,0,0,0,1,1,1,1,e,10,
  //   12,12,1,1,1,1,1,1
  //   contents of CM1 (hex, n*v repeats v):
  //   0,10,40,80,40,80,0,0,8,8,8,0,8,0,c,0,4,0,4,4,20,0,0,0,0,0,0,0,0,0,0,0,0,c,c,c,c,80,
  //   80,1,2,24,4,24,0,0,4
  //   contents of CM2 (hex, n*v repeats v):
  //   0,4,3,2,2,2,2,2,2,2,2,0,2,0,0,0,81,2,0,0,0,0,0,0,0,0,0,0,0,0,0,0,0,78,98,c8,18,80,
  //   c0,0,0,c0,80,0,0,0,2
  //   contents of CM3 (hex, n*v repeats v):
  //   0,0,10,10,20,10,0,0,10,10,10,0,10,0,20,0,e,80,0,0,10,0,0,0,0,0,0,0,0,0,0,0,0,a,9,
  //   e,8,e,f,0,0,f,e,40
  //   contents of CM4 (hex, n*v repeats v):
  //   c,0,40,40,40,40,6c,44,50,44,64,0,78,0,0,0,0,1,0,80,0,0,0,0,0,0,0,0,0,0,0,0,0,0,0,
  //   0,0,0,0,0,0,0,0,0,1,2
endmodule
